# Fritzing sketch Admin (saved by Fritzing 0.9.3b)
breadboards: 1

parts:
  HC-SR04_Sensor_1 = HC-SR04 Ultrasonic Distance Sensor
  HC-SR04_Sensor_2 = HC-SR04 Ultrasonic Distance Sensor
  J1 = Basic Servo
  M1 = DC Motor
  U1 = GAS_SENSOR [package=mq-3]
  U3 = ESP8266 NodeMCU LoLin module
  LED1 = smd LED [color="Green (570nm)" package="0805 [SMD]"]
  LED2 = smd LED [color="Red (633nm)" package="0805 [SMD]"]
  LED4 = smd LED [color="Red (633nm)" package="0805 [SMD]"]
  LED5 = smd LED [color="Green (560nm)" package="0805 [SMD]"]
  LED6 = smd LED [color="Red (633nm)" package="0805 [SMD]"]
  LED3 = smd LED [color="Green (565nm)" package="0805 [SMD]"]

nets:
  VCC: HC-SR04_Sensor_1.VCC, HC-SR04_Sensor_2.VCC, J1.vcc
  N1: HC-SR04_Sensor_1.TRIG, U3.D2
  N2: HC-SR04_Sensor_1.ECHO, U3.D3
  GND: HC-SR04_Sensor_1.GND, HC-SR04_Sensor_2.GND, J1.gnd, M1.pin_2, U1.H2, LED1.anode, LED2.anode, LED4.anode, LED5.anode, LED6.anode, LED3.anode
  N3: HC-SR04_Sensor_2.TRIG, U3.D1
  N4: HC-SR04_Sensor_2.ECHO, U3.D0
  N5: J1.pulse, U3.D7
  N6: M1.pin_1, U3.D6
  N7: U1.B1, U1.A1
  N8: U3.D4, LED5.cathode
  N9: U3.D5, LED6.cathode
  N10: U3.D8, LED4.cathode
  N11: U3.A0, LED1.cathode

custom parts:
  ESP8266 NodeMCU LoLin module: ESP8266 based NodeMCU
