# Fritzing sketch Untitled Sketch 2 (saved by Fritzing 0.9.3b)
circuit board: 8.46667cm x 5.64444cm
breadboards: 4

parts:
  Part1 = RFID-RC522-v2
  S1 = KY-026
  U1 = ESP8266 NodeMCU LoLin module
  LED1 = LED - 5mm [color="Red (633nm)" package="5 mm [THT]"]
  LED2 = smd LED [color="Green (570nm)" package="0603 [SMD]"]
  T1 = LM35 Temperature Sensor [package="TO92 [THT]"]
  J1 = Piezo Speaker
  Part2 = RFID-RC522-v2
  S2 = KY-026
  U2 = ESP8266 NodeMCU LoLin module
  LED3 = LED - 5mm [color="Red (633nm)" package="5 mm [THT]"]
  LED4 = smd LED [color="Green (570nm)" package="0603 [SMD]"]
  T2 = LM35 Temperature Sensor [package="TO92 [THT]"]
  J2 = Piezo Speaker
  Part3 = RFID-RC522-v2
  Part4 = RFID-RC522-v2
  S3 = KY-026
  S4 = KY-026
  U4 = ESP8266 NodeMCU LoLin module
  LED5 = LED - 5mm [color="Red (633nm)" package="5 mm [THT]"]
  LED6 = LED - 5mm [color="Red (633nm)" package="5 mm [THT]"]
  LED7 = smd LED [color="Green (570nm)" package="0603 [SMD]"]
  LED8 = smd LED [color="Green (570nm)" package="0603 [SMD]"]
  T3 = LM35 Temperature Sensor [package="TO92 [THT]"]
  T4 = LM35 Temperature Sensor [package="TO92 [THT]"]
  J3 = Piezo Speaker
  J4 = Piezo Speaker
  U3 = ESP8266 NodeMCU LoLin module

nets (from the breadboard view):
  N1: Part1.SDA, U1.D2
  N2: Part1.SCK, U1.D3
  N3: Part1.MOSI, U1.D4
  N4: Part1.MISO, U1.D5
  N5: Part1.IRQ, U1.D6
  GND: Part1.GND, S1.pin2, U1.GND, LED1.anode, LED2.anode, T1.GND, J1.pin1
  N6: Part1.RST, U1.D7
  3.3V: Part1.3.3V, S1.pin3, U1.3V3, T1.+Vs
  N7: S1.pin4, U1.D1
  N8: U1.D0, LED1.cathode, J1.pin2
  N9: U1.D8, LED2.cathode
  N10: U1.A0, T1.Vout
  N11: Part2.SDA, U2.D2
  N12: Part2.SCK, U2.D3
  N13: Part2.MOSI, U2.D4
  N14: Part2.MISO, U2.D5
  N15: Part2.IRQ, U2.D6
  GND_2: Part2.GND, S2.pin2, U2.GND, LED3.anode, LED4.anode, T2.GND, J2.pin1
  N16: Part2.RST, U2.D7
  3.3V_2: Part2.3.3V, S2.pin3, U2.3V3, T2.+Vs
  N17: S2.pin4, U2.D1
  N18: U2.D0, LED3.cathode, J2.pin2
  N19: U2.D8, LED4.cathode
  N20: U2.A0, T2.Vout
  N21: Part3.SDA, U4.D2
  N22: Part3.SCK, U4.D3
  N23: Part3.MOSI, U4.D4
  N24: Part3.MISO, U4.D5
  N25: Part3.IRQ, U4.D6
  GND_3: Part3.GND, S3.pin2, U4.GND, LED5.anode, LED7.anode, T4.GND, J4.pin1
  N26: Part3.RST, U4.D7
  3.3V_3: Part3.3.3V, S3.pin3, U4.3V3, T4.+Vs
  N27: Part4.SDA, U3.D2
  N28: Part4.SCK, U3.D3
  N29: Part4.MOSI, U3.D4
  N30: Part4.MISO, U3.D5
  N31: Part4.IRQ, U3.D6
  GND_4: Part4.GND, S4.pin2, LED6.anode, LED8.anode, T3.GND, J3.pin1, U3.GND
  N32: Part4.RST, U3.D7
  3.3V_4: Part4.3.3V, S4.pin3, T3.+Vs, U3.3V3
  N33: S3.pin4, U4.D1
  N34: S4.pin4, U3.D1
  N35: U4.D0, LED5.cathode, J4.pin2
  N36: U4.D8, LED7.cathode
  N37: U4.A0, T4.Vout
  N38: LED6.cathode, J3.pin2, U3.D0
  N39: LED8.cathode, U3.D8
  N40: T3.Vout, U3.A0

custom parts:
  RFID-RC522-v2: A simple China made RFID-RC522 Reader; do check the pin labels, as this is a MFRC522 based clone.
  KY-026: ky-026 flame sensor module
  ESP8266 NodeMCU LoLin module: ESP8266 based NodeMCU
